# Fritzing sketch 01 led (saved by Fritzing 0.8.0b)
breadboards: 1

parts:
  Composants1 = Arduino Uno (Rev3)
  LED1 = LED - 5mm [color="Red (633nm)" package="5 mm [THT]"]
  R1 = Resistor [tolerance=±5% resistance=220 package=THT]

nets:
  N1: Composants1.D13/SCK, LED1.anode
  N2: LED1.cathode, R1.Pin_0
